# Fritzing sketch spritelet2-itsybitsy (saved by Fritzing 0.9.2b)
circuit board: 4.318cm x 4.445cm

parts:
  VS = female pin header, 2 pins [form="♀ (female)"]
  J4 = female pin header, 2 pins [form="♀ (female)"]
  J5 = female pin header, 3 pins [form="♀ (female)"]
  RT = female pin header, 1 pin [form="♀ (female)"]
  LT = female pin header, 1 pin [form="♀ (female)"]
  POWER = Toggle Switch [package=THT]
  J7 = female pin header, 14 pins [form="♀ (female)"]
  J1 = female pin header, 11 pins [form="♀ (female)"]
  J8 = female pin header, 3 pins [form="♀ (female)"]  # not connected
  J9 = female pin header, 9 pins [form="♀ (female)"]
  UP = female pin header, 1 pin [form="♀ (female)"]
  DN = female pin header, 1 pin [form="♀ (female)"]
  CT = female pin header, 1 pin [form="♀ (female)"]
  CM = female pin header, 1 pin [form="♀ (female)"]

nets:
  N1: VS.pin1, J5.pin2, J7.pin2, J1.pin3, CM.pin1
  N2: VS.pin2, J7.pin9
  N3: J4.pin1, POWER.L2
  N4: J4.pin2, POWER.COM
  N5: J5.pin1, J7.pin1, J1.pin1
  N6: J5.pin3, J7.pin3
  N7: RT.pin1, J9.pin5
  N8: LT.pin1, J9.pin4
  N9: J7.pin4, J1.pin11
  N10: J7.pin5, J1.pin10
  N11: J7.pin6, J1.pin9
  N12: J7.pin7, J1.pin8
  N13: J7.pin8, J1.pin7
  N14: J1.pin4, J9.pin6
  N15: J1.pin5, J9.pin8
  N16: J1.pin6, J9.pin7
  N17: J9.pin1, CT.pin1
  N18: J9.pin2, UP.pin1
  N19: J9.pin3, DN.pin1

notes:
  USB Side
  Pin Side
  < Adafruit ItsyBitsy >
  Adafruit
  LiPoly
  Backpack
  /\
  \/
  < Adafruit 1.44" TFT Backpack >
  SLET-ITSY-B
