# Fritzing sketch spritelet2-nano (saved by Fritzing 0.9.2b)
circuit board: 4.318cm x 4.445cm

parts:
  VS = female pin header, 2 pins [form="♀ (female)"]
  J4 = female pin header, 2 pins [form="♀ (female)"]
  J5 = female pin header, 3 pins [form="♀ (female)"]
  RT = female pin header, 1 pin [form="♀ (female)"]
  LT = female pin header, 1 pin [form="♀ (female)"]
  POWER = Toggle Switch [package=THT]
  J1 = female pin header, 11 pins [form="♀ (female)"]
  Part1 = Arduino Nano (Rev3.0)
  VUSB = female pin header, 1 pin [form="♀ (female)"]
  UP = female pin header, 1 pin [form="♀ (female)"]
  DN = female pin header, 1 pin [form="♀ (female)"]
  CT = female pin header, 1 pin [form="♀ (female)"]
  CM = female pin header, 1 pin [form="♀ (female)"]

nets:
  N1: VS.pin1, Part1.D4
  N2: VS.pin2, Part1.D3
  N3: J4.pin1, POWER.L2
  N4: J4.pin2, POWER.COM
  N5: J5.pin1, J1.pin1, Part1.VIN
  N6: J5.pin2, J1.pin3, Part1.GND
  N7: J5.pin3, VUSB.pin1
  N8: RT.pin1, Part1.A5
  N9: LT.pin1, Part1.A4
  N10: J1.pin4, Part1.D13/SCK
  N11: J1.pin5, Part1.D12/MISO
  N12: J1.pin6, Part1.D11/MOSI
  N13: J1.pin7, Part1.D10
  N14: J1.pin8, Part1.D6
  N15: J1.pin9, Part1.D8
  N16: J1.pin10, Part1.D5
  N17: J1.pin11, Part1.D9
  N18: Part1.A3, DN.pin1
  N19: Part1.A2, UP.pin1
  N20: Part1.A1, CT.pin1
  N21: Part1.A0, CM.pin1

notes:
  USB Side
  ICSP Side
  < Arduino Nano >
  Adafruit
  LiPoly
  Backpack
  /\
  \/
  < Adafruit 1.44" TFT Backpack >
  SLET-NANO-B
